# Fritzing sketch Untitled Sketch (saved by Fritzing 0.9.3b)
circuit board: 8.46667cm x 5.64444cm
breadboards: 1

parts:
  Charli = Adafruit CharliePlex Driver IS31FL3731 [part_number="Adafruit #2946"]
  Raspberry_Pi_1 = Raspberry Pi 3 [part_number=RPI-3-V1.2]

nets:
  N1: Charli.SDA, Raspberry_Pi_1.GPIO2
  3V3: Charli.SHUTDOWN, Raspberry_Pi_1.3v3, Raspberry_Pi_1.3V3
  N2: Charli.AUDIOIN, Raspberry_Pi_1.GPIO3
  N3: Charli.INTB, Raspberry_Pi_1.GND

custom parts:
  Adafruit CharliePlex Driver IS31FL3731: The IS31FL3731 will let you get back to that classic LED matrix look, with a nice upgrade! This I2C LED driver chip has the ability to PWM each individual LED in a 16x9 grid so you can have beautiful LED lighting effects, without a lot of pin twiddling. Simply tell the chip which LED on the grid you want lit, and what brightness and it's all taken care of for you. The IS31FL3731 is a nice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
